# Fritzing sketch simon_sketch (saved by Fritzing 0.9.2b)
breadboards: 1

parts:
  Part1 = Arduino Uno (Rev3)
  LED1 = LED - 5mm [color="Red (633nm)" package="5 mm [THT]"]
  LED2 = LED - 5mm [color="Blue (470nm)" package="5 mm [THT]"]
  LED3 = LED - 5mm [color="Yellow (585nm)" package="5 mm [THT]"]
  LED4 = LED - 5mm [color="Green (560nm)" package="5 mm [THT]"]
  R3 = Resistor [tolerance=±5% resistance=10k package=THT]
  R4 = Resistor [tolerance=±5% resistance=10k package=THT]
  R1 = Resistor [tolerance=±5% resistance=10k package=THT]
  R5 = Resistor [tolerance=±5% resistance=220 package=THT]
  R6 = Resistor [tolerance=±5% resistance=10k package=THT]
  R7 = Resistor [tolerance=±5% resistance=220 package="2010 [SMD]"]
  R8 = Resistor [tolerance=±5% resistance=220 package="2010 [SMD]"]
  R9 = Resistor [tolerance=±5% resistance=220 package="2010 [SMD]"]
  S2 = Pushbutton [package="[THT]"]
  S1 = Pushbutton [package="[THT]"]
  S3 = Pushbutton [package="[THT]"]
  S4 = Pushbutton [package="[THT]"]

nets:
  N1: Part1.D8, R5.Pin_1
  N2: Part1.D9_PWM, R3.Pin_0, S3.Pin_3, S3.Pin_4
  N3: Part1.D10_PWM/SS, R7.Pin_1
  N4: Part1.D11_PWM/MOSI, R4.Pin_0, S4.Pin_3, S4.Pin_4
  N5: Part1.D12/MISO, R8.Pin_1
  N6: Part1.GND, LED1.cathode, LED2.cathode, LED3.cathode, LED4.cathode, R3.Pin_1, R4.Pin_1, R1.Pin_1, R6.Pin_1
  N7: Part1.D5_PWM, R6.Pin_0, S1.Pin_3, S1.Pin_4
  N8: Part1.D6_PWM, R9.Pin_1
  N9: Part1.D7, R1.Pin_0, S2.Pin_3, S2.Pin_4
  N10: Part1.5V, S2.Pin_1, S2.Pin_2, S1.Pin_1, S1.Pin_2, S3.Pin_1, S3.Pin_2, S4.Pin_1, S4.Pin_2
  N11: LED1.anode, R9.Pin_0
  N12: LED2.anode, R8.Pin_0
  N13: LED3.anode, R5.Pin_0
  N14: LED4.anode, R7.Pin_0
